# Fritzing sketch control (saved by Fritzing 0.9.3b)
breadboards: 1

parts:
  Raspberry_Pi_1 = Raspberry Pi 4 [part_number=RPI-4-b]
  Transceiver1 = nRF24L01 [package=module]
  VCC1 = Battery block 9V

nets:
  3V3: Raspberry_Pi_1.3v3, Transceiver1.VCC
  N1: Raspberry_Pi_1.GPIO22, Transceiver1.CE
  N2: Raspberry_Pi_1.GPIO10, Transceiver1.MOSI
  N3: Raspberry_Pi_1.GPIO9, Transceiver1.MISO
  N4: Raspberry_Pi_1.GPIO11, Transceiver1.SCK
  N5: Raspberry_Pi_1.GPIO8, Transceiver1.CSN
  GND: Raspberry_Pi_1.GND, Transceiver1.GND, VCC1.-
  N6: Raspberry_Pi_1.5V, VCC1.+

custom parts:
  Raspberry Pi 4: The RPi4, a faster version of the awesome Raspberry Pi 2 B ARM Board with 40 pin gpio. Ready for special Raspberry Pi B+ and RPi2 Hat (Hardware attached (on) top)
  nRF24L01: nRF24L01 module
