# Fritzing sketch robot-pico (saved by Fritzing 0.9.3b)
breadboards: 1

parts:
  Mod1 = Raspberry Pi Pico
  M1 = fc-51 [package=THT]
  M2 = fc-51 [package=THT]
  M3 = fc-51 [package=THT]
  M4 = fc-51 [package=THT]
  Transceiver1 = nRF24L01 [package=module]
  Mod2 = L298N DC motor driver
  M5 = DC Motor
  M6 = DC Motor
  VCC1 = Battery block 9V
  LED1 = LEDs [package=led10mm]
  LED2 = LEDs [package=led10mm]
  LED3 = LEDs [package=led10mm]
  R1 = Resistor [tolerance=±5% resistance=220 package=THT]
  R2 = Resistor [tolerance=±5% resistance=220 package=THT]
  R3 = Resistor [tolerance=±5% resistance=220 package=THT]

nets:
  N1: Mod1.pin_1, R3.Pin_0
  N2: Mod1.pin_2, R2.Pin_0
  N3: Mod1.pin_3, Mod1.pin_8, Mod1.pin_18, Mod1.pin_23, Mod1.pin_38, M1.pin2, M2.pin2, M3.pin2, M4.pin2, Transceiver1.GND, LED1.C, LED2.C, LED3.C
  N4: Mod1.pin_4, Transceiver1.CE
  N5: Mod1.pin_5, Transceiver1.CSN
  N6: Mod1.pin_6, R1.Pin_0
  N7: Mod1.pin_9, Mod2.ENA
  N8: Mod1.pin_10, Mod2.IN1
  N9: Mod1.pin_11, Mod2.IN2
  N10: Mod1.pin_14, Mod2.ENB
  N11: Mod1.pin_15, Mod2.IN3
  N12: Mod1.pin_16, Mod2.IN4
  N13: Mod1.pin_17, M1.pin1
  N14: Mod1.pin_19, M2.pin1
  N15: Mod1.pin_20, M3.pin1
  N16: Mod1.pin_21, Transceiver1.MISO
  N17: Mod1.pin_22, M4.pin1
  N18: Mod1.pin_24, Transceiver1.SCK
  N19: Mod1.pin_25, Transceiver1.MOSI
  N20: Mod1.pin_36, M1.pin3, M2.pin3, M3.pin3, M4.pin3, Transceiver1.VCC
  N21: Mod2.OUT1, M5.pin_1
  N22: Mod2.OUT2, M5.pin_2
  N23: Mod2.12V, Mod2.5V-ENA-JMP-I, VCC1.+
  N24: Mod2.GND, VCC1.-
  N25: Mod2.OUT3, M6.pin_1
  N26: Mod2.OUT4, M6.pin_2
  N27: LED1.A, R1.Pin_1
  N28: LED2.A, R2.Pin_1
  N29: LED3.A, R3.Pin_1

custom parts:
  Raspberry Pi Pico: Raspberry Pi Pico. Based around the RP2040 microcontroller the Pico is a low cost microcontroller device bringing Raspberry Pi quality, cost, and easy of use to the microcontroller space. Jan 2021, Split part in to two versions: tht (this one) and SMD. This one will drill holes for a .1 in header in pcb to allow plugging in the module as well as providing pads to solder the module to the top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
  nRF24L01: nRF24L01 module
  L298N DC motor driver: 2x DC motor driver with 78M05 positive voltage regulator (7..35 V) L298N: max 46 V, 2 A Set 5 V Enable jumper to enable 5 V regultor (needed for the L298N) and +5 V output at screw terminal or supply external +5 V at screw terminal Set ENA and/or ENB to +5 V to enable motor permanently or supply ENA and/or ENB with PWM signal IN1 and IN2 set rotation directory for motor A (OUT1/OUT2) IN2 and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
